# Fritzing sketch elBanquos christmas light_MK2 (saved by Fritzing 0.9.10b)
circuit board: 5.1cm x 3.6cm
breadboards: 1

parts:
  LED_1_1 = ws2812b [package="smd 2812b"]
  P1 = male pin header, 3 pins [form="♂ (male)"]
  LED_1_2 = ws2812b [package="smd 2812b"]
  LED_1_3 = ws2812b [package="smd 2812b"]
  LED_1_4 = ws2812b [package="smd 2812b"]
  LED_1_5 = ws2812b [package="smd 2812b"]
  LED_1_6 = ws2812b [package="smd 2812b"]
  LED_1_7 = ws2812b [package="smd 2812b"]
  LED_1_8 = ws2812b [package="smd 2812b"]
  LED_2_8 = ws2812b [package="smd 2812b"]
  LED_2_5 = ws2812b [package="smd 2812b"]
  LED_2_4 = ws2812b [package="smd 2812b"]
  LED_2_2 = ws2812b [package="smd 2812b"]
  LED_2_7 = ws2812b [package="smd 2812b"]
  LED_2_3 = ws2812b [package="smd 2812b"]
  LED_2_6 = ws2812b [package="smd 2812b"]
  LED_2_1 = ws2812b [package="smd 2812b"]
  LED_3_4 = ws2812b [package="smd 2812b"]
  LED_3_7 = ws2812b [package="smd 2812b"]
  LED_3_2 = ws2812b [package="smd 2812b"]
  LED_3_1 = ws2812b [package="smd 2812b"]
  LED_3_6 = ws2812b [package="smd 2812b"]
  LED_3_3 = ws2812b [package="smd 2812b"]
  LED_3_8 = ws2812b [package="smd 2812b"]
  LED_3_5 = ws2812b [package="smd 2812b"]
  P2 = male pin header, 3 pins [form="♂ (male)"]
  P3 = male pin header, 3 pins [form="♂ (male)"]
  S2 = female pin header, 3 pins [form="♀ (female)"]
  S1 = female pin header, 3 pins [form="♀ (female)"]
  S3 = female pin header, 3 pins [form="♀ (female)"]
  Bauteil2 = Arduino Nano (Rev3.0)
  X1 = USB Connectors [package=usb-a-pcb]
  Step_Button = Pushbutton [package="[THT]"]
  Mode_Button = Pushbutton [package="[THT]"]
  R1 = Resistor [tolerance=±5% power=0.25 resistance=10k package=THT]
  PR = Photocell (LDR) [package=THT]
  Day/Night_threshold1 = Rotary Potentiometer (Small) [maximum_resistance=10kΩ knob_status=50% power=0.5W package=THT]
  C1 = Electrolytic Capacitor [capacitance=1mF voltage=35V package="200 mil [THT, electrolytic]"]

nets:
  VDD: LED_1_1.VDD, P1.pin2, LED_1_2.VDD, LED_1_3.VDD, LED_1_4.VDD, LED_1_5.VDD, LED_1_6.VDD, LED_1_7.VDD, LED_1_8.VDD, LED_2_8.VDD, LED_2_5.VDD, LED_2_4.VDD, LED_2_2.VDD, LED_2_7.VDD, LED_2_3.VDD, LED_2_6.VDD, LED_2_1.VDD, LED_3_4.VDD, LED_3_7.VDD, LED_3_2.VDD, LED_3_1.VDD, LED_3_6.VDD, LED_3_3.VDD, LED_3_8.VDD, LED_3_5.VDD, P2.pin2, P3.pin2, S2.pin2, S1.pin2, S3.pin2, Bauteil2.5V, X1.VBUS, PR.pin_1, Day/Night_threshold1.leg1, C1.+
  N1: LED_1_1.DOUT, LED_1_2.DIN
  VSS: LED_1_1.VSS, P1.pin3, LED_1_2.VSS, LED_1_3.VSS, LED_1_4.VSS, LED_1_5.VSS, LED_1_6.VSS, LED_1_7.VSS, LED_1_8.VSS, LED_2_8.VSS, LED_2_5.VSS, LED_2_4.VSS, LED_2_2.VSS, LED_2_7.VSS, LED_2_3.VSS, LED_2_6.VSS, LED_2_1.VSS, LED_3_4.VSS, LED_3_7.VSS, LED_3_2.VSS, LED_3_1.VSS, LED_3_6.VSS, LED_3_3.VSS, LED_3_8.VSS, LED_3_5.VSS, P2.pin3, P3.pin3, S2.pin3, S1.pin3, S3.pin3, Bauteil2.GND, X1.GND, Step_Button.Pin_1, Step_Button.Pin_2, Mode_Button.Pin_1, Mode_Button.Pin_2, R1.Pin_1, Day/Night_threshold1.leg2, C1.-
  N2: LED_1_1.DIN, P1.pin1, S1.pin1, Bauteil2.D7
  N3: LED_1_2.DOUT, LED_1_3.DIN
  N4: LED_1_3.DOUT, LED_1_4.DIN
  N5: LED_1_4.DOUT, LED_1_5.DIN
  N6: LED_1_5.DOUT, LED_1_6.DIN
  N7: LED_1_6.DOUT, LED_1_7.DIN
  N8: LED_1_7.DOUT, LED_1_8.DIN
  N9: LED_2_8.DIN, LED_2_7.DOUT
  N10: LED_2_5.DOUT, LED_2_6.DIN
  N11: LED_2_5.DIN, LED_2_4.DOUT
  N12: LED_2_4.DIN, LED_2_3.DOUT
  N13: LED_2_2.DOUT, LED_2_3.DIN
  N14: LED_2_2.DIN, LED_2_1.DOUT
  N15: LED_2_7.DIN, LED_2_6.DOUT
  N16: LED_2_1.DIN, P2.pin1, S2.pin1, Bauteil2.D8
  N17: LED_3_4.DOUT, LED_3_5.DIN
  N18: LED_3_4.DIN, LED_3_3.DOUT
  N19: LED_3_7.DOUT, LED_3_8.DIN
  N20: LED_3_7.DIN, LED_3_6.DOUT
  N21: LED_3_2.DOUT, LED_3_3.DIN
  N22: LED_3_2.DIN, LED_3_1.DOUT
  N23: LED_3_1.DIN, P3.pin1, S3.pin1, Bauteil2.D9
  N24: LED_3_6.DIN, LED_3_5.DOUT
  N25: Bauteil2.D2, Step_Button.Pin_3, Step_Button.Pin_4
  N26: Bauteil2.D3, Mode_Button.Pin_3, Mode_Button.Pin_4
  N27: Bauteil2.A1, Day/Night_threshold1.wiper
  N28: Bauteil2.A0, R1.Pin_0, PR.pin_0

notes:
  Cable piece
  ABCDEFGHIJKLMNOPQRST
  0102030405060708091011121314
